# Fritzing sketch skema (saved by Fritzing 0.9.3b)

parts:
  Part1 = Arduino Nano (Rev3.0)
  SIM800L_BO1 = SIM800L BO
  Part2 = u-blox NEO-6M GPS Breakout
  D1 = Diode [package=diode-1n4001]
  C1 = Electrolytic Capacitor [capacitance=1000μF package="1010 [SMD, electrolytic]"]
  BAT1 = BC9VPC [package=bc9vpc]

nets:
  GND: Part1.GND, Part2.GND, C1.-
  N1: Part1.D2, SIM800L_BO1.PIN3
  N2: Part1.D3, SIM800L_BO1.PIN2
  N3: Part1.D4, SIM800L_BO1.pin_4
  N4: Part1.D8, Part2.RXD
  N5: Part1.D9, Part2.TXD
  N6: Part1.VIN, BAT1.V+
  N7: Part1.5V, D1.A
  N8: D1.C, C1.+
